# Fritzing sketch Steppermotor_Steuerung_Teil1 (saved by Fritzing 0.9.3b)
breadboards: 2

parts:
  Nano_V2 = Nano V3
  Pololu_A1 = Pololu A4988 [package=SO16]
  U1 = POT [package=pot_alpha_rv16af-20]
  M1 = Stepper Motor - Bipolar
  R1 = Resistor [tolerance=±1% resistance=2.2k package="0603 [SMD]"]
  YwRobot_Power_Supply1 = YwRobot Breadboard Power Supply [part_number=545043]
  JACK2 = 2.1mm Barrel Jack with Terminal Block

nets:
  GND: Nano_V2.GND, Pololu_A1.GND, U1.E, YwRobot_Power_Supply1.GND#13, YwRobot_Power_Supply1.GND#14, JACK2.NEG
  N1: Nano_V2.D6, Pololu_A1.ENABLE, R1.Pin_1
  N2: Nano_V2.D7, Pololu_A1.DIR
  N3: Nano_V2.D8, Pololu_A1.STEP
  N4: Nano_V2.D10, Pololu_A1.MS1
  N5: Nano_V2.D11/MOSI, Pololu_A1.MS2
  N6: Nano_V2.D12/MISO, Pololu_A1.MS3
  5V: Nano_V2.5V, Pololu_A1.VDD, U1.A, R1.Pin_0, YwRobot_Power_Supply1.VCC#9, YwRobot_Power_Supply1.VCC#10
  N7: Nano_V2.A0, U1.S
  N8: Pololu_A1.RESET, Pololu_A1.SLEEP
  N9: Pololu_A1.1B, M1.D
  N10: Pololu_A1.1A, M1.B
  N11: Pololu_A1.2A, M1.C
  N12: Pololu_A1.2B, M1.A
  N13: Pololu_A1.VMOT, JACK2.POS
  N14: YwRobot_Power_Supply1.VCC#5, YwRobot_Power_Supply1.VCC#6
  N15: YwRobot_Power_Supply1.GND#11, YwRobot_Power_Supply1.GND#12

custom parts:
  Nano V3: Can be used universally thanks to a compact design! By 14 digital in - and outputs and 6 analog inputs on the Nano V3 can also be used for larger projects! Thanks to the ATmega328 micro-controller, as well as more sophisticated programs to be executable! By Arduino compatibility in the Arduino IDE programmable! With FTDI Chip! Usual high quality and fast delivery directly from Germany by order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
  YwRobot Breadboard Power Supply: The YwRobot Breadboard Power Supply (MB-V2) has two power rails; they can be 5V or 3V3. Power to the module can be provided through the female USB socket or through the A10 (female) 2.1mm power jack.
